# Fritzing sketch LightGary (saved by Fritzing 0.9.2b)
circuit board: 17.0429cm x 8.56423cm
breadboards: 2

parts:
  Bauteil1 = Arduino Uno (Rev3)
  SW1 = ENCODER_RGB_CA [package=encoder_led_3]  # not connected
  LED1 = RGB LED - (4 legs) [package="5 mm [THT]"]
  ENCODER1 = Rotary Encoder with Knob  # not connected
  U1 = 74HC595 [package="DIP16 [THT]"]
  RTC1 = DS1307 RTC Breakout
  U2 = 74HC595 [package="DIP16 [THT]"]
  U3 = 74HC595 [package="DIP16 [THT]"]
  R1 = Resistor [tolerance=±2% resistance=270 package=THT]
  R2 = Resistor [tolerance=±2% resistance=270 package=THT]
  R3 = Resistor [tolerance=±2% resistance=270 package=THT]
  R4 = Resistor [tolerance=±2% resistance=270 package=THT]
  R5 = Resistor [tolerance=±2% resistance=270 package=THT]
  R6 = Resistor [tolerance=±2% resistance=270 package=THT]
  R7 = Resistor [tolerance=±2% resistance=270 package=THT]
  R8 = Resistor [tolerance=±2% resistance=270 package=THT]
  R9 = Resistor [tolerance=±2% resistance=270 package=THT]
  R10 = Resistor [tolerance=±2% resistance=270 package=THT]
  R11 = Resistor [tolerance=±2% resistance=270 package=THT]
  C1 = Electrolytic Capacitor [capacitance=1mF package="100 mil [THT, electrolytic]"]
  R12 = Resistor [tolerance=±5% resistance=330 package=THT]
  R13 = Resistor [tolerance=±5% resistance=330 package=THT]
  R14 = Resistor [tolerance=±5% resistance=330 package=THT]
  J1 = female pin header, 8 pins [form="♀ (female)"]
  J3 = female pin header, 8 pins [form="♀ (female)"]  # not connected

nets:
  VCC: Bauteil1.5V, LED1.common_anode, U1.MR, U1.VCC, RTC1.5V, U2.MR, U2.VCC, U3.MR, U3.VCC, C1.+
  GND: Bauteil1.GND, U1.GND, U1.OE, RTC1.GND, U2.GND, U2.OE, U3.GND, U3.OE, R1.Pin_1, C1.-
  N1: LED1.red_cathode, R12.Pin_0
  N2: LED1.green_cathode, R14.Pin_0
  N3: LED1.blue_cathode, R13.Pin_0
  N4: U2.Q5, R1.Pin_0
  N5: U2.Q6, R4.Pin_0
  N6: U2.Q7, R3.Pin_0
  N7: U3.Q1, R2.Pin_0
  N8: U3.Q2, R9.Pin_0
  N9: U3.Q3, R8.Pin_0
  N10: U3.Q4, R7.Pin_0
  N11: U3.Q5, R6.Pin_0
  N12: U3.Q6, R5.Pin_0
  N13: U3.Q7, R11.Pin_1
  N14: U3.Q0, R10.Pin_1
  N15: R2.Pin_1, J1.pin2
  N16: R5.Pin_1, J1.pin7
  N17: R6.Pin_1, J1.pin6
  N18: R7.Pin_1, J1.pin5
  N19: R8.Pin_1, J1.pin4
  N20: R9.Pin_1, J1.pin3
  N21: R10.Pin_0, J1.pin1
  N22: R11.Pin_0, J1.pin8

custom parts:
  Rotary Encoder with Knob: Rotary Encoder with 1/4" Shaft and Knob
  DS1307 RTC Breakout: DS1307 Real-time Clock Breakout Board with Battery
